// Logisim project 8bitregister.circ as structural Verilog: 1 circuit, main circuit 8bitregister
module _8bitregister (
  input  EN,
  input  [7:0] I,
  input  [1:0] FunSel,
  input  Clock,
  output [7:0] Q
);

  wire and_1_out;
  wire [7:0] adder_1_out, multiplexer_1_out, subtractor_1_out;

  and and_1 (and_1_out, FunSel[0], FunSel[1]);
  D_Flip_Flop d_ff_1 (.clk(Clock), .D(multiplexer_1_out[5]), .Q(Q[5]), .en(EN), .reset(and_1_out));  // open: Qn, preset
  D_Flip_Flop d_ff_2 (.clk(Clock), .D(multiplexer_1_out[4]), .Q(Q[4]), .en(EN), .reset(and_1_out));  // open: Qn, preset
  D_Flip_Flop d_ff_3 (.clk(Clock), .D(multiplexer_1_out[3]), .Q(Q[3]), .en(EN), .reset(and_1_out));  // open: Qn, preset
  D_Flip_Flop d_ff_4 (.clk(Clock), .D(multiplexer_1_out[2]), .Q(Q[2]), .en(EN), .reset(and_1_out));  // open: Qn, preset
  D_Flip_Flop d_ff_5 (.clk(Clock), .D(multiplexer_1_out[1]), .Q(Q[1]), .en(EN), .reset(and_1_out));  // open: Qn, preset
  D_Flip_Flop d_ff_6 (.clk(Clock), .D(multiplexer_1_out[0]), .Q(Q[0]), .en(EN), .reset(and_1_out));  // open: Qn, preset
  D_Flip_Flop d_ff_7 (.clk(Clock), .D(multiplexer_1_out[6]), .Q(Q[6]), .en(EN), .reset(and_1_out));  // open: Qn, preset
  D_Flip_Flop d_ff_8 (.clk(Clock), .D(multiplexer_1_out[7]), .Q(Q[7]), .en(EN), .reset(and_1_out));  // open: Qn, preset
  Multiplexer #(.select(2), .width(8)) multiplexer_1 (
    .in0(subtractor_1_out), .in1(adder_1_out), .in2(I), .in3({8{1'b0}}), .out(multiplexer_1_out),
    .sel(FunSel), .en(EN));
  Subtractor subtractor_1 (.a(Q), .b(8'h1), .out(subtractor_1_out));  // open: bin, bout
  Adder adder_1 (.a(Q), .b(8'h1), .out(adder_1_out));  // open: cin, cout
endmodule
