// Logisim project IR.circ as structural Verilog: 1 circuit, main circuit main
module main (
  input  [7:0] I1,
  input  [1:0] FunSel,
  input  Enable,
  input  LH,
  input  CLOCK,
  output [15:0] IRout
);

  wire and_1_out, and_2_out, clear, multiplexer_1_out, multiplexer_2_out, not_1_out;
  wire [7:0] least, most, multiplexer_3_out, multiplexer_4_out;
  wire [15:0] adder_1_out, inter, multiplexer_5_out, subtractor_1_out;

  and and_1 (and_1_out, Enable, LH);
  not not_1 (not_1_out, LH);
  and and_2 (and_2_out, Enable, not_1_out);
  Multiplexer #(.select(2), .enable("false")) multiplexer_1 (
    .in0(Enable), .in1(Enable), .in2(and_1_out), .in3(and_1_out), .out(multiplexer_1_out), .sel(FunSel));
  Multiplexer #(.select(2), .enable("false")) multiplexer_2 (
    .in0(Enable), .in1(Enable), .in2(and_2_out), .in3(and_2_out), .out(multiplexer_2_out), .sel(FunSel));
  Multiplexer #(.select(2), .width(8), .enable("false")) multiplexer_3 (
    .in0(least), .in1(least), .in2(I1), .in3(I1), .out(multiplexer_3_out), .sel(FunSel));
  Multiplexer #(.select(2), .width(8), .enable("false")) multiplexer_4 (
    .in0(most), .in1(most), .in2(I1), .in3(I1), .out(multiplexer_4_out), .sel(FunSel));
  D_Flip_Flop d_ff_1 (
    .clk(CLOCK), .D(multiplexer_3_out[0]), .Q(inter[0]), .en(multiplexer_1_out), .reset(clear));  // open: Qn, preset
  D_Flip_Flop d_ff_2 (
    .clk(CLOCK), .D(multiplexer_3_out[1]), .Q(inter[1]), .en(multiplexer_1_out), .reset(clear));  // open: Qn, preset
  D_Flip_Flop d_ff_3 (
    .clk(CLOCK), .D(multiplexer_3_out[2]), .Q(inter[2]), .en(multiplexer_1_out), .reset(clear));  // open: Qn, preset
  D_Flip_Flop d_ff_4 (
    .clk(CLOCK), .D(multiplexer_3_out[3]), .Q(inter[3]), .en(multiplexer_1_out), .reset(clear));  // open: Qn, preset
  D_Flip_Flop d_ff_5 (
    .clk(CLOCK), .D(multiplexer_3_out[4]), .Q(inter[4]), .en(multiplexer_1_out), .reset(clear));  // open: Qn, preset
  D_Flip_Flop d_ff_6 (
    .clk(CLOCK), .D(multiplexer_3_out[5]), .Q(inter[5]), .en(multiplexer_1_out), .reset(clear));  // open: Qn, preset
  D_Flip_Flop d_ff_7 (
    .clk(CLOCK), .D(multiplexer_3_out[6]), .Q(inter[6]), .en(multiplexer_1_out), .reset(clear));  // open: Qn, preset
  D_Flip_Flop d_ff_8 (
    .clk(CLOCK), .D(multiplexer_3_out[7]), .Q(inter[7]), .en(multiplexer_1_out), .reset(clear));  // open: Qn, preset
  D_Flip_Flop d_ff_9 (
    .clk(CLOCK), .D(multiplexer_4_out[0]), .Q(inter[8]), .en(multiplexer_2_out), .reset(clear));  // open: Qn, preset
  D_Flip_Flop d_ff_10 (
    .clk(CLOCK), .D(multiplexer_4_out[1]), .Q(inter[9]), .en(multiplexer_2_out), .reset(clear));  // open: Qn, preset
  D_Flip_Flop d_ff_11 (
    .clk(CLOCK), .D(multiplexer_4_out[2]), .Q(inter[10]), .en(multiplexer_2_out), .reset(clear));  // open: Qn, preset
  D_Flip_Flop d_ff_12 (
    .clk(CLOCK), .D(multiplexer_4_out[3]), .Q(inter[11]), .en(multiplexer_2_out), .reset(clear));  // open: Qn, preset
  D_Flip_Flop d_ff_13 (
    .clk(CLOCK), .D(multiplexer_4_out[4]), .Q(inter[12]), .en(multiplexer_2_out), .reset(clear));  // open: Qn, preset
  D_Flip_Flop d_ff_14 (
    .clk(CLOCK), .D(multiplexer_4_out[5]), .Q(inter[13]), .en(multiplexer_2_out), .reset(clear));  // open: Qn, preset
  D_Flip_Flop d_ff_15 (
    .clk(CLOCK), .D(multiplexer_4_out[6]), .Q(inter[14]), .en(multiplexer_2_out), .reset(clear));  // open: Qn, preset
  D_Flip_Flop d_ff_16 (
    .clk(CLOCK), .D(multiplexer_4_out[7]), .Q(inter[15]), .en(multiplexer_2_out), .reset(clear));  // open: Qn, preset
  and and_3 (clear, FunSel[0], FunSel[1]);
  Subtractor #(.width(16)) subtractor_1 (.a(IRout), .b(16'h1), .out(subtractor_1_out));  // open: bin, bout
  Adder #(.width(16)) adder_1 (.a(16'h1), .b(IRout), .out(adder_1_out));  // open: cin, cout
  Multiplexer #(.select(3), .width(16), .enable("false")) multiplexer_5 (
    .in0({most, least}), .in1({most, least}), .in2({most, least}), .in3({most, least}),
    .in4({I1, IRout[7:0]}), .in5({IRout[15:8], I1}), .in6({most, least}), .in7({most, least}),
    .out(multiplexer_5_out), .sel({FunSel, LH}));
  _16_bitd_main main_1 (.Input(multiplexer_5_out), .Output(IRout), .Clock(CLOCK), .CLR(clear), .EN(Enable));
  Multiplexer #(.select(2), .width(16), .enable("false")) multiplexer_6 (
    .in0(subtractor_1_out), .in1(adder_1_out), .in2(inter), .in3(inter), .out({most, least}), .sel(FunSel));
  Hex_Digit_Display hex_digit_display_1 (.value(IRout[15:12]));  // open: dp
  Hex_Digit_Display hex_digit_display_2 (.value(IRout[11:8]));  // open: dp
  Hex_Digit_Display hex_digit_display_3 (.value(IRout[7:4]));  // open: dp
  Hex_Digit_Display hex_digit_display_4 (.value(IRout[3:0]));  // open: dp

  // Other names for the same wires on the sheet: EN = Enable; inter2[15:0] = IRout; inter2L[7:0] = IRout[7:0];
  //   inter2H[7:0] = IRout[15:8]
endmodule
