// Logisim project alu.circ as structural Verilog: 1 circuit, main circuit main
module main (
  input  [7:0] A,
  input  [7:0] B,
  input  [3:0] FunSel,
  input  Clock,
  output [7:0] OutALU,
  output [3:0] OutFlag__ZCNO
);

  wire and_1_out, and_2_out, and_3_out, and_4_out, comparator_1_lt, main_1_a___b___cin_cout,
       main_1_a___b_cout, main_1_a___b_cout_2, or_1_out, or_2_out, xor_1_out;
  wire [7:0] main_1_a___b, main_1_a___b_2, main_1_a___b___carry, main_1_a_and_b, main_1_a_or_b,
       main_1_a_xor_b, n8bitregister_1_q, not_1_out, not_2_out, shifter_1_out, shifter_2_out, shifter_3_out,
       shifter_4_out, shifter_5_out, shifter_6_out;
  wire [7:4] undriven;

  operations_main main_1 (
    .Cin(n8bitregister_1_q[2]), .A(A), .B(B), .A___B(main_1_a___b), .A___B_COUT(main_1_a___b_cout),
    .A___B___Carry(main_1_a___b___carry), .A___B___cin_COUT(main_1_a___b___cin_cout),
    .A___B_2(main_1_a___b_2), .A___B_COUT_2(main_1_a___b_cout_2), .A_or_B(main_1_a_or_b),
    .A_and_B(main_1_a_and_b), .A_xor_B(main_1_a_xor_b));
  Shifter #(.shift("rl")) shifter_1 (.in(A), .\dist (3'b001), .out(shifter_1_out));
  Shifter #(.shift("rr")) shifter_2 (.in(A), .\dist (3'b001), .out(shifter_2_out));
  Shifter shifter_3 (.in(A), .\dist (3'b001), .out(shifter_3_out));
  Shifter #(.shift("lr")) shifter_4 (.in(A), .\dist (3'b001), .out(shifter_4_out));
  Shifter #(.shift("ar")) shifter_5 (.in(A), .\dist (3'b001), .out(shifter_5_out));
  Shifter shifter_6 (.in(A), .\dist (3'b001), .out(shifter_6_out));
  assign not_1_out = ~A;  // NOT_Gate not_1, 8 bits wide
  assign not_2_out = ~B;  // NOT_Gate not_2, 8 bits wide
  Multiplexer #(.select(4), .width(8), .enable("false")) multiplexer_1 (
    .in0(A), .in1(B), .in2(not_1_out), .in3(not_2_out), .in4(main_1_a___b), .in5(main_1_a___b___carry),
    .in6(main_1_a___b_2), .in7(main_1_a_and_b), .in8(main_1_a_or_b), .in9(main_1_a_xor_b),
    .in10(shifter_3_out), .in11(shifter_4_out), .in12(shifter_6_out), .in13(shifter_5_out),
    .in14(shifter_1_out), .in15(shifter_2_out), .out(OutALU), .sel(FunSel));
  Multiplexer #(.select(4), .enable("false")) multiplexer_2 (
    .in4(main_1_a___b_cout), .in5(main_1_a___b___cin_cout), .in6(main_1_a___b_cout_2), .in10(A[7]),
    .in11(A[0]), .in14(A[7]), .in15(A[0]), .out(OutFlag__ZCNO[2]), .sel(FunSel));  // open: in0, in1, in2, in3, in7, in8, in9, in12, in13
  and and_1 (and_1_out, ~A[7], ~B[7], OutALU[7]);  // AND_Gate
  and and_2 (and_2_out, A[7], B[7], ~OutALU[7]);  // AND_Gate
  and and_3 (and_3_out, ~A[7], B[7], OutALU[7]);  // AND_Gate
  and and_4 (and_4_out, A[7], ~B[7], ~OutALU[7]);  // AND_Gate
  xor xor_1 (xor_1_out, A[7], A[6]);
  or or_1 (or_1_out, and_1_out, and_2_out);
  or or_2 (or_2_out, and_3_out, and_4_out);
  Hex_Digit_Display hex_digit_display_1 (.value(OutALU[7:4]));  // open: dp
  Multiplexer #(.select(4), .enable("false")) multiplexer_3 (
    .in4(or_1_out), .in5(or_1_out), .in6(or_2_out), .in12(xor_1_out), .out(OutFlag__ZCNO[0]), .sel(FunSel));  // open: in0, in1, in2, in3, in7, in8, in9, in10, in11, in13, in14, in15
  Hex_Digit_Display hex_digit_display_2 (.value(OutALU[3:0]));  // open: dp
  Comparator comparator_1 (.a(OutALU), .b({8{1'b0}}), .eq(OutFlag__ZCNO[3]), .lt(comparator_1_lt));  // open: gt
  Multiplexer #(.select(4), .enable("false")) multiplexer_4 (
    .in0(comparator_1_lt), .in1(comparator_1_lt), .in2(comparator_1_lt), .in3(comparator_1_lt),
    .in4(comparator_1_lt), .in5(comparator_1_lt), .in6(comparator_1_lt), .in7(comparator_1_lt),
    .in8(comparator_1_lt), .in9(comparator_1_lt), .in10(comparator_1_lt), .in11(comparator_1_lt),
    .in12(comparator_1_lt), .in14(comparator_1_lt), .in15(comparator_1_lt), .out(OutFlag__ZCNO[1]),
    .sel(FunSel));  // open: in13
  _8bitregister u_8bitregister_1 (
    .EN(1'b1), .I({undriven, OutFlag__ZCNO}), .FunSel(2'b10), .Clock(Clock), .Q(n8bitregister_1_q));

  // Other names for the same wires on the sheet: O = OutFlag__ZCNO[0]; N = OutFlag__ZCNO[1]; C = OutFlag__ZCNO[2];
  //   Z = OutFlag__ZCNO[3]; A_LSB = A[0]; A_SSB = A[6]; A_MSB = A[7]; B_MSB = B[7]; Out_MSB = OutALU[7]

  // Notes on the sheet:
  //   CSL
  //   CSR
  //   LSL
  //   LSR
  //   ASR
  //   ASL
endmodule
