// Logisim project part4.circ as structural Verilog: 1 circuit, main circuit main
module main (
  input  [2:0] OutASel,
  input  [2:0] OutBSel,
  input  [3:0] FunSelAlu,
  input  [1:0] FunSel,
  input  [3:0] RegSel,
  input  [3:0] TempSel,
  input  [1:0] MuxASel,
  input  [1:0] OutCSel,
  input  in_9,
  input  in_10,
  input  in_11,
  input  [1:0] MuxBSel,
  input  [1:0] OutDSel,
  input  [1:0] FunSel_2,
  input  [2:0] RegSel_2,
  input  Enable,
  input  LH,
  input  [1:0] FunSel_3,
  output [3:0] ZCNO,
  output [7:0] IR8_15,
  output [7:0] IR0_7
);

  wire CLOCK_out;
  wire [7:0] ARF_outc, ARF_outd, main_1_outalu, multiplexer_1_out, multiplexer_2_out, ram_1_data,
       registerfile_1_outa, registerfile_1_outb;

  Clock CLOCK (.out(CLOCK_out));
  registerfile registerfile_1 (
    .I(multiplexer_1_out), .OutASel(OutASel), .OutBSel(OutBSel), .FunSel(FunSel), .RegSel(RegSel),
    .TmpSel(TempSel), .Clock(CLOCK_out), .OutA(registerfile_1_outa), .OutB(registerfile_1_outb));
  Multiplexer #(.select(2), .width(8), .enable("false")) multiplexer_1 (
    .in0(main_1_outalu), .in1(ARF_outc), .in2(ram_1_data), .in3(IR0_7), .out(multiplexer_1_out), .sel(MuxASel));
  IR_main IR (.I1(ram_1_data), .Enable(Enable), .LH(LH), .CLOCK(CLOCK_out), .FunSel(FunSel_3), .IRout({IR8_15, IR0_7}));
  alu_main main_1 (
    .A(registerfile_1_outa), .B(registerfile_1_outb), .FunSel(FunSelAlu), .Clock(CLOCK_out),
    .OutALU(main_1_outalu), .OutFlag__ZCNO(ZCNO));
  Multiplexer #(.select(2), .width(8), .enable("false")) multiplexer_2 (
    .in0(ARF_outc), .in1(main_1_outalu), .in2(ram_1_data), .in3(IR0_7), .out(multiplexer_2_out), .sel(MuxBSel));
  address_register_file ARF (
    .I(multiplexer_2_out), .OutCSel(OutCSel), .OutDSel(OutDSel), .FunSel(FunSel_2), .RegSel(RegSel_2),
    .Clock(CLOCK_out), .OutC(ARF_outc), .OutD(ARF_outd));
  RAM #(.bus("separate")) ram_1 (
    .addr(ARF_outd), .din(main_1_outalu), .data(ram_1_data), .str(in_9), .clk(CLOCK_out), .ld(in_10),
    .clr(in_11));  // open: sel
endmodule
