// Logisim project 16 bitd.circ as structural Verilog: 1 circuit, main circuit main
module main (
  input  [15:0] Input,
  input  Clock,
  input  CLR,
  input  EN,
  output [15:0] Output
);

  D_Flip_Flop d_ff_1 (.clk(Clock), .D(Input[15]), .Q(Output[15]), .en(EN), .reset(CLR));  // open: Qn, preset
  D_Flip_Flop d_ff_2 (.clk(Clock), .D(Input[13]), .Q(Output[13]), .en(EN), .reset(CLR));  // open: Qn, preset
  D_Flip_Flop d_ff_3 (.clk(Clock), .D(Input[14]), .Q(Output[14]), .en(EN), .reset(CLR));  // open: Qn, preset
  D_Flip_Flop d_ff_4 (.clk(Clock), .D(Input[12]), .Q(Output[12]), .en(EN), .reset(CLR));  // open: Qn, preset
  D_Flip_Flop d_ff_5 (.clk(Clock), .D(Input[11]), .Q(Output[11]), .en(EN), .reset(CLR));  // open: Qn, preset
  D_Flip_Flop d_ff_6 (.clk(Clock), .D(Input[10]), .Q(Output[10]), .en(EN), .reset(CLR));  // open: Qn, preset
  D_Flip_Flop d_ff_7 (.clk(Clock), .D(Input[9]), .Q(Output[9]), .en(EN), .reset(CLR));  // open: Qn, preset
  D_Flip_Flop d_ff_8 (.clk(Clock), .D(Input[8]), .Q(Output[8]), .en(EN), .reset(CLR));  // open: Qn, preset
  D_Flip_Flop d_ff_9 (.clk(Clock), .D(Input[7]), .Q(Output[7]), .en(EN), .reset(CLR));  // open: Qn, preset
  D_Flip_Flop d_ff_10 (.clk(Clock), .D(Input[5]), .Q(Output[5]), .en(EN), .reset(CLR));  // open: Qn, preset
  D_Flip_Flop d_ff_11 (.clk(Clock), .D(Input[6]), .Q(Output[6]), .en(EN), .reset(CLR));  // open: Qn, preset
  D_Flip_Flop d_ff_12 (.clk(Clock), .D(Input[4]), .Q(Output[4]), .en(EN), .reset(CLR));  // open: Qn, preset
  D_Flip_Flop d_ff_13 (.clk(Clock), .D(Input[3]), .Q(Output[3]), .en(EN), .reset(CLR));  // open: Qn, preset
  D_Flip_Flop d_ff_14 (.clk(Clock), .D(Input[2]), .Q(Output[2]), .en(EN), .reset(CLR));  // open: Qn, preset
  D_Flip_Flop d_ff_15 (.clk(Clock), .D(Input[1]), .Q(Output[1]), .en(EN), .reset(CLR));  // open: Qn, preset
  D_Flip_Flop d_ff_16 (.clk(Clock), .D(Input[0]), .Q(Output[0]), .en(EN), .reset(CLR));  // open: Qn, preset
endmodule
