// Logisim project Project2.circ as structural Verilog: 1 circuit, main circuit main
// OutASel
module main (
  input  Clear,
  output [3:0] ZCNO,
  output [7:0] IR8_15,
  output [7:0] IR0_7
);

  wire CLOCK_out, IREN, LH, Load, Store;
  wire [1:0] FunSelARF, FunSelIR, FunSelRF, MuxASel, MuxBSel, OutCSel, OutDSel;
  wire [2:0] OutASel, OutBSel, RegSelARF;
  wire [3:0] FunSelALU, RegSelRF, TempSel;
  wire [7:0] ARF_outc, ARF_outd, main_1_outalu, multiplexer_1_out, multiplexer_2_out, ram_1_data,
       registerfile_1_outa, registerfile_1_outb;

  Clock CLOCK (.out(CLOCK_out));
  registerfile registerfile_1 (
    .I(multiplexer_1_out), .OutASel(OutASel), .OutBSel(OutBSel), .FunSel(FunSelRF), .RegSel(RegSelRF),
    .TmpSel(TempSel), .Clock(CLOCK_out), .OutA(registerfile_1_outa), .OutB(registerfile_1_outb));
  Multiplexer #(.select(2), .width(8), .enable("false")) multiplexer_1 (
    .in0(main_1_outalu), .in1(ARF_outc), .in2(ram_1_data), .in3(IR0_7), .out(multiplexer_1_out), .sel(MuxASel));
  IR_main IR (.I1(ram_1_data), .Enable(IREN), .LH(LH), .CLOCK(CLOCK_out), .FunSel(FunSelIR), .IRout({IR8_15, IR0_7}));
  alu_main main_1 (
    .A(registerfile_1_outa), .B(registerfile_1_outb), .FunSel(FunSelALU), .Clock(CLOCK_out),
    .OutALU(main_1_outalu), .OutFlag__ZCNO(ZCNO));
  Multiplexer #(.select(2), .width(8), .enable("false")) multiplexer_2 (
    .in0(ARF_outc), .in1(main_1_outalu), .in2(ram_1_data), .in3(IR0_7), .out(multiplexer_2_out), .sel(MuxBSel));
  address_register_file ARF (
    .I(multiplexer_2_out), .OutCSel(OutCSel), .OutDSel(OutDSel), .FunSel(FunSelARF), .RegSel(RegSelARF),
    .Clock(CLOCK_out), .OutC(ARF_outc), .OutD(ARF_outd));
  RAM #(.bus("separate")) ram_1 (
    .addr(ARF_outd), .din(main_1_outalu), .data(ram_1_data), .str(Store), .clk(CLOCK_out), .ld(Load),
    .clr(Clear));  // open: sel
  control_unit_main main_2 (
    .CLK(CLOCK_out), .Z(ZCNO[3]), .IR({IR8_15, IR0_7}), .LH(LH), .IREN(IREN), .FunselIR(FunSelIR),
    .Store(Store), .OutputMuxASel(MuxASel), .FunSelARF(FunSelARF), .OutputMuxBSel(MuxBSel), .Load(Load),
    .OutputBSel(OutBSel), .OutputASel(OutASel), .OutputFunSelAlu(FunSelALU), .FunSelRF(FunSelRF),
    .OutputDSel(OutDSel), .RegSelARF(RegSelARF), .OutputCSel(OutCSel), .TempSel(TempSel), .RegselRF(RegSelRF));

  // Other names for the same wires on the sheet: IR[15:0] = {IR8_15, IR0_7}; Z = ZCNO[3]
endmodule
