// Logisim project address_register_file.circ as structural Verilog: 1 circuit, main circuit address register file
module address_register_file (
  input  [7:0] I,
  input  [1:0] OutCSel,
  input  [1:0] OutDSel,
  input  [1:0] FunSel,
  input  [2:0] RegSel,
  input  Clock,
  output [7:0] OutC,
  output [7:0] OutD
);

  wire not_1_out, not_2_out, not_3_out;
  wire [7:0] AR_q, PC_q, SR_q;

  not not_1 (not_1_out, RegSel[2]);
  not not_2 (not_2_out, RegSel[1]);
  not not_3 (not_3_out, RegSel[0]);
  _8bitregister PC (.EN(not_1_out), .I(I), .FunSel(FunSel), .Clock(Clock), .Q(PC_q));
  _8bitregister AR (.EN(not_2_out), .I(I), .FunSel(FunSel), .Clock(Clock), .Q(AR_q));
  _8bitregister SR (.EN(not_3_out), .I(I), .FunSel(FunSel), .Clock(Clock), .Q(SR_q));
  Hex_Digit_Display hex_digit_display_1 (.value(OutC[7:4]));  // open: dp
  Multiplexer #(.select(2), .width(8)) multiplexer_1 (
    .in0(PC_q), .in1(PC_q), .in2(AR_q), .in3(SR_q), .out(OutC), .sel(OutCSel), .en(1'b1));
  Multiplexer #(.select(2), .width(8)) multiplexer_2 (
    .in0(PC_q), .in1(PC_q), .in2(AR_q), .in3(SR_q), .out(OutD), .sel(OutDSel), .en(1'b1));
  Hex_Digit_Display hex_digit_display_2 (.value(OutC[3:0]));  // open: dp
  Hex_Digit_Display hex_digit_display_3 (.value(OutD[7:4]));  // open: dp
  Hex_Digit_Display hex_digit_display_4 (.value(OutD[3:0]));  // open: dp
endmodule
