// Logisim project control unit.circ as structural Verilog: 1 circuit, main circuit main
// Control Unit
module main (
  input  CLK,
  input  Z,
  input  [15:0] IR,
  output Store,
  output [1:0] OutputMuxASel,
  output [1:0] FunSelARF,
  output [1:0] OutputMuxBSel,
  output Load,
  output [2:0] OutputBSel,
  output [2:0] OutputASel,
  output [3:0] OutputFunSelAlu,
  output [1:0] FunSelRF,
  output [1:0] OutputDSel,
  output LH,
  output IREN,
  output [1:0] FunselIR,
  output [2:0] RegSelARF,
  output [1:0] OutputCSel,
  output [3:0] TempSel,
  output [3:0] RegselRF
);

  wire and_1_out, and_2_out, and_3_out, and_4_out, and_5_out, and_6_out, and_7_out, and_8_out, and_9_out,
       and_10_out, and_11_out, and_12_out, and_13_out, and_14_out, and_15_out, and_16_out, and_17_out,
       and_18_out, and_19_out, and_20_out, and_21_out, and_22_out, and_23_out, and_24_out, and_25_out,
       and_26_out, and_27_out, and_28_out, and_29_out, and_30_out, and_31_out, and_32_out, and_33_out,
       and_34_out, and_35_out, and_36_out, and_37_out, and_38_out, and_39_out, and_40_out, and_41_out,
       and_42_out, and_43_out, and_44_out, and_45_out, and_46_out, and_47_out, and_48_out, and_49_out,
       and_50_out, and_51_out, and_52_out, and_53_out, and_54_out, and_55_out, and_56_out, and_57_out,
       and_58_out, and_59_out, and_60_out, and_61_out, and_62_out, and_63_out, and_64_out, and_65_out,
       and_66_out, and_67_out, and_68_out, and_69_out, and_70_out, and_71_out, and_72_out, and_73_out,
       and_74_out, and_75_out, and_76_out, and_77_out, and_78_out, and_79_out, and_80_out, and_81_out,
       and_82_out, and_83_out, and_84_out, and_85_out, and_86_out, and_87_out, and_88_out, and_89_out,
       and_90_out, and_91_out, and_92_out, and_93_out, and_94_out, and_95_out, and_96_out, and_97_out,
       and_98_out, and_99_out, and_100_out, and_101_out, and_102_out, and_103_out, and_104_out, and_105_out,
       and_106_out, and_107_out, and_108_out, and_109_out, and_110_out, and_111_out, and_112_out,
       and_113_out, and_114_out, and_115_out, and_116_out, and_117_out, and_118_out, and_119_out,
       and_120_out, and_121_out, and_122_out, and_123_out, and_124_out, and_125_out, and_126_out,
       and_127_out, and_128_out, and_129_out, and_130_out, and_131_out, and_132_out, and_133_out,
       and_134_out, and_135_out, and_136_out, and_137_out, and_138_out, and_139_out, and_140_out,
       and_141_out, and_142_out, and_143_out, and_144_out, and_145_out, and_146_out, and_147_out,
       and_148_out, and_149_out, and_150_out, and_151_out, and_152_out, and_153_out, and_154_out,
       and_155_out, and_156_out, and_157_out, and_158_out, and_159_out, and_160_out, and_161_out,
       and_162_out, and_163_out, and_164_out, and_165_out, and_166_out, and_167_out, and_168_out,
       and_169_out, and_170_out, and_171_out, and_172_out, and_173_out, and_174_out, and_175_out,
       and_176_out, and_177_out, and_178_out, and_179_out, and_180_out, and_181_out, and_182_out,
       and_183_out, and_184_out, and_185_out, and_186_out, and_187_out, and_188_out, and_189_out,
       and_190_out, and_191_out, and_192_out, and_193_out, and_194_out, and_195_out, and_196_out,
       and_197_out, and_198_out, and_199_out, and_200_out, and_201_out, and_202_out, and_203_out,
       and_204_out, and_205_out, and_206_out, and_207_out, and_208_out, and_209_out, and_210_out,
       and_211_out, and_212_out, and_213_out, and_214_out, and_215_out, and_216_out, and_217_out,
       and_218_out, and_219_out, and_220_out, and_221_out, and_222_out, and_223_out, and_224_out,
       and_225_out, and_226_out, and_227_out, and_228_out, and_229_out, and_230_out, and_231_out,
       and_232_out, and_233_out, and_234_out, and_235_out, and_236_out, and_237_out, and_238_out,
       and_239_out, and_240_out, and_241_out, and_242_out, and_243_out, and_244_out, and_245_out,
       and_246_out, and_247_out, and_248_out, and_249_out, and_250_out, and_251_out, and_252_out,
       and_253_out, and_254_out, and_255_out, and_256_out, and_257_out, and_258_out, and_259_out,
       and_260_out, and_261_out, and_262_out, and_263_out, and_264_out, and_265_out, and_266_out,
       and_267_out, and_268_out, and_269_out, and_270_out, and_271_out, and_272_out, and_273_out,
       and_274_out, and_275_out, and_276_out, and_277_out, and_278_out, and_279_out, and_280_out,
       and_281_out, and_282_out, and_283_out, and_284_out, and_285_out, and_286_out, and_287_out,
       and_288_out, and_289_out, and_290_out, and_291_out, and_292_out, and_293_out, and_294_out,
       and_295_out, and_296_out, and_297_out, and_298_out, and_299_out, and_300_out, and_301_out,
       and_302_out, and_303_out, and_304_out, and_305_out, and_306_out, and_307_out, and_308_out,
       and_309_out, and_310_out, and_311_out, and_312_out, and_313_out, and_314_out, and_315_out,
       and_316_out, D0, D0_D12_D13_D14, D1, D1_D13_D14, D2, D3, D3_D6_D9_D10,
       D3_D6_D9_D10_D11_D13IR10_D14IR10, D3_D6_D9_D10_D13_D14, D3_D13_D14, D4, D4___D5___D7, D4___D5___D7_D8,
       D4_D5_D7_D8, D5, D6, D7, D8, D9, D10, D11, D12, D13, D13_D14, D14, D15, d_ff_1_q, nand_3_out, NotSTR,
       or_1_out, or_2_out, or_3_out, or_4_out, or_5_out, or_6_out, or_7_out, or_8_out, or_9_out, or_10_out,
       or_11_out, or_12_out, or_13_out, or_14_out, or_15_out, or_16_out, or_17_out, or_18_out, or_19_out,
       or_20_out, or_27_out, or_28_out, or_29_out, or_30_out, or_31_out, or_32_out, or_35_out, or_36_out,
       or_37_out, or_38_out, or_39_out, or_40_out, or_41_out, or_42_out, or_43_out, or_44_out, or_45_out,
       or_46_out, or_47_out, or_48_out, or_49_out, or_50_out, or_52_out, or_53_out, or_54_out, or_55_out,
       or_56_out, or_57_out, or_58_out, or_59_out, or_60_out, or_61_out, or_62_out, or_63_out, or_64_out,
       or_66_out, or_67_out, or_70_out, or_71_out, or_72_out, or_73_out, or_74_out, or_75_out, or_76_out,
       or_78_out, or_79_out, or_80_out, or_81_out, or_82_out, or_83_out, or_84_out, or_85_out, or_86_out,
       or_89_out, or_90_out, or_91_out, or_92_out, or_93_out, or_94_out, or_95_out, or_96_out, or_99_out,
       or_100_out, or_101_out, or_102_out, or_103_out, or_104_out, or_105_out, SC, T0, T1, T2, T3, T4, T4_T5,
       T5, T6, T7, xor_1_out, xor_2_out, xor_3_out;
  wire [1:0] DecodedIR54ARF, DecodedIR98ARF;
  wire [2:0] counter_1_q;
  wire [3:0] DecodedIR54, DecodedIR98, decoder_2_out3, decoder_3_out3;

  xor xor_1 (xor_1_out, IR[6], IR[2]);
  or or_1 (or_1_out, D14, D13);
  and and_1 (and_1_out, D0, T4);
  and and_2 (and_2_out, D0, T5);
  and and_3 (and_3_out, D4_D5_D7_D8, T4, ~IR[10], IR[6], IR[2]);  // AND_Gate
  and and_4 (and_4_out, D4_D5_D7_D8, T5, ~IR[10], xor_1_out);  // AND_Gate
  and and_5 (and_5_out, D4_D5_D7_D8, T6, ~IR[10], ~IR[6], ~IR[2]);  // AND_Gate
  and and_6 (and_6_out, D3_D6_D9_D10, T4, IR[6], ~IR[10]);  // AND_Gate
  and and_7 (and_7_out, D3_D6_D9_D10, T5, ~IR[6], ~IR[10]);  // AND_Gate
  and and_8 (and_8_out, D12, T5, ~IR[10]);  // AND_Gate
  and and_9 (and_9_out, or_1_out, T4, ~IR[10]);  // AND_Gate
  and and_10 (and_10_out, D15, T4);
  and and_11 (and_11_out, D4, IR[10], ~IR[2], T4, IR[6]);  // AND_Gate
  and and_12 (and_12_out, D4, ~IR[10], ~IR[2], T4, IR[6]);  // AND_Gate
  and and_13 (and_13_out, D5, IR[10], ~IR[2], T4, IR[6]);  // AND_Gate
  and and_14 (and_14_out, D5, ~IR[10], ~IR[2], T4, IR[6]);  // AND_Gate
  and and_15 (and_15_out, D7, IR[10], ~IR[2], T4, IR[6]);  // AND_Gate
  and and_16 (and_16_out, D7, ~IR[10], ~IR[2], T4, IR[6]);  // AND_Gate
  and and_17 (and_17_out, D8, IR[10], ~IR[2], T4, IR[6]);  // AND_Gate
  and and_18 (and_18_out, D11, T6);
  and and_19 (and_19_out, D14, T5, ~IR[10]);  // AND_Gate
  and and_20 (and_20_out, D12, T4);
  and and_21 (and_21_out, D13, T5, ~IR[10]);  // AND_Gate
  and and_22 (and_22_out, D4, ~IR[10], ~IR[2], T5, ~IR[6]);  // AND_Gate
  and and_23 (and_23_out, D5, ~IR[10], ~IR[2], T5, ~IR[6]);  // AND_Gate
  and and_24 (and_24_out, D7, ~IR[10], ~IR[2], T5, ~IR[6]);  // AND_Gate
  and and_25 (and_25_out, D8, ~IR[10], ~IR[2], T4, IR[6]);  // AND_Gate
  and and_26 (and_26_out, D8, ~IR[10], ~IR[2], T5, ~IR[6]);  // AND_Gate
  and and_27 (and_27_out, D11, T4, ~IR[6]);  // AND_Gate
  or or_2 (or_2_out, and_18_out, and_19_out);
  assign FunSelARF = or_2_out ? 2'b00 : 2'bz;  // Controlled_Buffer controlled_buffer_1
  or or_3 (or_3_out, T1, T3, and_20_out, and_21_out);
  assign FunSelARF = or_3_out ? 2'b01 : 2'bz;  // Controlled_Buffer controlled_buffer_2
  or or_4 (or_4_out, and_2_out, and_3_out, and_4_out, and_5_out, and_6_out, and_7_out, and_8_out, and_9_out, and_10_out);
  assign FunSelARF = or_4_out ? 2'b10 : 2'bz;  // Controlled_Buffer controlled_buffer_3
  and and_28 (and_28_out, D3, ~IR[10], T4, ~IR[6]);  // AND_Gate
  and and_29 (and_29_out, D9, ~IR[10], T4, ~IR[6]);  // AND_Gate
  and and_30 (and_30_out, D4, IR[10], IR[2], T4, ~IR[6]);  // AND_Gate
  and and_31 (and_31_out, D5, IR[10], IR[2], T4, ~IR[6]);  // AND_Gate
  and and_32 (and_32_out, D7, IR[10], IR[2], T4, ~IR[6]);  // AND_Gate
  and and_33 (and_33_out, D8, IR[10], IR[2], T4, ~IR[6]);  // AND_Gate
  and and_34 (and_34_out, D4, ~IR[10], IR[2], T4, ~IR[6]);  // AND_Gate
  and and_35 (and_35_out, D5, ~IR[10], IR[2], T4, ~IR[6]);  // AND_Gate
  and and_36 (and_36_out, D7, ~IR[10], IR[2], T4, ~IR[6]);  // AND_Gate
  and and_37 (and_37_out, D6, ~IR[10], T4, ~IR[6]);  // AND_Gate
  and and_38 (and_38_out, D10, ~IR[10], T4, ~IR[6]);  // AND_Gate
  and and_39 (and_39_out, D5, IR[10], ~IR[2], T4, ~IR[6]);  // AND_Gate
  and and_40 (and_40_out, D8, ~IR[10], IR[2], T4, ~IR[6]);  // AND_Gate
  Decoder #(.select(3), .enable("false")) decoder_1 (
    .out0(T0), .out1(T1), .out2(T2), .out3(T3), .out4(T4), .out5(T5), .out6(T6), .out7(T7), .sel(counter_1_q));
  Counter #(.width(3), .max('h7)) counter_1 (
    .count(1'b1), .Q(counter_1_q), .clk(CLK), .clr(d_ff_1_q));  // open: load, D, carry
  and and_41 (and_41_out, D12, T5, ~IR[10]);  // AND_Gate
  or or_5 (or_5_out, and_1_out, and_28_out, and_37_out, and_38_out, and_29_out);
  and and_42 (and_42_out, D4, IR[10], ~IR[2], T4, ~IR[6]);  // AND_Gate
  and and_43 (and_43_out, D7, IR[10], ~IR[2], T4, ~IR[6]);  // AND_Gate
  and and_44 (and_44_out, D8, IR[10], ~IR[2], T4, ~IR[6]);  // AND_Gate
  D_Flip_Flop d_ff_1 (.clk(CLK), .D(SC), .Q(d_ff_1_q), .en(1'b1), .reset(d_ff_1_q));  // open: Qn, preset
  xor xor_2 (xor_2_out, IR[6], IR[2]);
  and and_45 (and_45_out, D4, ~IR[10], ~IR[2], T4, ~IR[6]);  // AND_Gate
  and and_46 (and_46_out, D5, ~IR[10], ~IR[2], T4, ~IR[6]);  // AND_Gate
  and and_47 (and_47_out, D7, ~IR[10], ~IR[2], T4, ~IR[6]);  // AND_Gate
  and and_48 (and_48_out, D8, ~IR[10], ~IR[2], T4, ~IR[6]);  // AND_Gate
  and and_49 (and_49_out, D4_D5_D7_D8, T4, ~IR[10], IR[6], IR[2]);  // AND_Gate
  and and_50 (and_50_out, D4_D5_D7_D8, T5, ~IR[10], xor_2_out);  // AND_Gate
  and and_51 (and_51_out, D4_D5_D7_D8, T6, ~IR[10], ~IR[6], ~IR[2]);  // AND_Gate
  and and_52 (and_52_out, D3_D6_D9_D10, T4, IR[6], ~IR[10]);  // AND_Gate
  and and_53 (and_53_out, D3_D6_D9_D10, T5, ~IR[6], ~IR[10]);  // AND_Gate
  and and_54 (and_54_out, D13_D14, T4_T5, ~IR[10]);  // AND_Gate
  or or_6 (or_6_out, or_5_out, or_7_out, or_8_out, or_9_out, or_13_out);
  and and_55 (and_55_out, D4, IR[10], ~IR[2], T5, ~IR[6]);  // AND_Gate
  and and_56 (and_56_out, D5, IR[10], ~IR[2], T5, ~IR[6]);  // AND_Gate
  and and_57 (and_57_out, D7, IR[10], ~IR[2], T5, ~IR[6]);  // AND_Gate
  and and_58 (and_58_out, D8, IR[10], ~IR[2], T5, ~IR[6]);  // AND_Gate
  and and_59 (and_59_out, D0, T5);
  and and_60 (and_60_out, D11, T6);
  and and_61 (and_61_out, D12, T4);
  assign RegselRF = or_6_out ? 4'b1111 : 4'bz;  // Controlled_Buffer controlled_buffer_4
  or or_7 (or_7_out, and_11_out, and_30_out, and_42_out, and_55_out, and_45_out, and_34_out, and_12_out, and_22_out);
  or or_8 (or_8_out, and_13_out, and_31_out, and_39_out, and_56_out, and_46_out, and_35_out, and_14_out, and_23_out);
  or or_9 (or_9_out, and_15_out, and_32_out, and_43_out, and_57_out, and_47_out, and_36_out, and_16_out, and_24_out);
  or or_10 (or_10_out, T1, T3, and_59_out);
  or or_11 (or_11_out, and_60_out, and_61_out);
  or or_12 (or_12_out, and_49_out, and_50_out, and_51_out, and_41_out, and_52_out, and_53_out, and_54_out);
  assign RegSelARF = or_12_out ? {IR[9], DecodedIR98ARF} : 3'bz;  // Controlled_Buffer controlled_buffer_5
  and and_62 (and_62_out, D15, T4);
  or or_13 (or_13_out, and_17_out, and_33_out, and_44_out, and_58_out, and_27_out, and_48_out, and_40_out, and_25_out, and_26_out);
  assign RegSelARF = or_10_out ? 3'b011 : 3'bz;  // Controlled_Buffer controlled_buffer_6
  assign RegSelARF = or_11_out ? 3'b110 : 3'bz;  // Controlled_Buffer controlled_buffer_7
  assign RegSelARF = and_62_out ? {Z, 2'b11} : 3'bz;  // Controlled_Buffer controlled_buffer_8
  or or_14 (or_14_out, or_16_out, or_17_out, or_18_out, and_97_out, or_19_out, or_20_out, or_15_out);
  assign RegselRF = or_14_out ? DecodedIR98 : 4'bz;  // Controlled_Buffer controlled_buffer_9
  or or_15 (or_15_out, and_101_out, and_95_out, and_93_out, and_76_out, and_77_out, and_88_out, and_96_out, and_102_out);
  or or_16 (or_16_out, and_83_out, and_63_out, and_64_out, and_89_out, and_65_out, and_90_out, and_91_out, and_66_out, and_67_out, and_92_out);
  or or_17 (or_17_out, and_94_out, and_68_out, and_69_out, and_84_out);
  or or_18 (or_18_out, and_98_out, and_70_out, and_71_out, and_85_out);
  or or_19 (or_19_out, and_99_out, and_72_out, and_73_out, and_86_out);
  or or_20 (or_20_out, and_100_out, and_74_out, and_75_out, and_87_out);
  or or_21 (D0_D12_D13_D14, D0, D12, D13, D14);
  or or_22 (D4_D5_D7_D8, D4, D5, D7, D8);
  or or_23 (D3_D6_D9_D10, D3, D6, D9, D10);
  or or_24 (D13_D14, D13, D14);
  or or_25 (D1_D13_D14, D1, D13, D14);
  or or_26 (T4_T5, T4, T5);
  and and_63 (and_63_out, D1, T5, ~IR[10]);  // AND_Gate
  and and_64 (and_64_out, D3, T4, IR[6], IR[10]);
  and and_65 (and_65_out, D3, T4, ~IR[6], IR[10]);  // AND_Gate
  and and_66 (and_66_out, D9, T4, IR[6], IR[10]);
  and and_67 (and_67_out, D9, T4, ~IR[6], IR[10]);  // AND_Gate
  and and_68 (and_68_out, D4, T4, IR[2], IR[6], IR[10]);
  and and_69 (and_69_out, D4, T6, ~IR[2], ~IR[6], IR[10]);  // AND_Gate
  and and_70 (and_70_out, D5, T4, IR[2], IR[6], IR[10]);
  and and_71 (and_71_out, D5, T6, ~IR[2], ~IR[6], IR[10]);  // AND_Gate
  and and_72 (and_72_out, D7, T4, IR[2], IR[6], IR[10]);
  and and_73 (and_73_out, D7, T6, ~IR[2], ~IR[6], IR[10]);  // AND_Gate
  and and_74 (and_74_out, D8, T4, IR[2], IR[6], IR[10]);
  and and_75 (and_75_out, D8, T6, ~IR[2], ~IR[6], IR[10]);  // AND_Gate
  and and_76 (and_76_out, D13, T4, IR[6], IR[10]);
  and and_77 (and_77_out, D14, T4, IR[6], IR[10]);
  and and_78 (and_78_out, D2, T4);
  and and_79 (and_79_out, D11, T4, IR[6]);
  and and_80 (and_80_out, D11, T5, ~IR[6]);  // AND_Gate
  and and_81 (and_81_out, D1, T4, ~IR[10]);  // AND_Gate
  and and_82 (and_82_out, D12, T5);
  and and_83 (and_83_out, D1, T4);
  not not_1 (NotSTR, or_27_out);
  or or_27 (or_27_out, and_78_out, and_79_out, and_80_out);
  assign Store = or_27_out ? 1'b1 : 1'bz;  // Controlled_Buffer controlled_buffer_10
  or or_28 (or_28_out, T0, T2, and_81_out, and_82_out);
  assign Load = or_28_out ? 1'b1 : 1'bz;  // Controlled_Buffer controlled_buffer_11
  assign LH = T0 ? 1'b1 : 1'bz;  // Controlled_Buffer controlled_buffer_12
  assign LH = T2 ? 1'b0 : 1'bz;  // Controlled_Buffer controlled_buffer_13
  and and_84 (and_84_out, D4, T5, ~IR[2], IR[6], IR[10]);  // AND_Gate
  and and_85 (and_85_out, D5, T5, ~IR[2], IR[6], IR[10]);  // AND_Gate
  and and_86 (and_86_out, D7, T5, ~IR[2], IR[6], IR[10]);  // AND_Gate
  and and_87 (and_87_out, D8, T5, ~IR[2], IR[6], IR[10]);  // AND_Gate
  and and_88 (and_88_out, D14, T5, IR[6], IR[10]);
  assign Store = NotSTR ? 1'b0 : 1'bz;  // Controlled_Buffer controlled_buffer_14
  and and_89 (and_89_out, D6, T4, IR[6], IR[10]);
  and and_90 (and_90_out, D6, T4, ~IR[6], IR[10]);  // AND_Gate
  and and_91 (and_91_out, D10, T4, IR[6], IR[10]);
  and and_92 (and_92_out, D10, T4, ~IR[6], IR[10]);  // AND_Gate
  and and_93 (and_93_out, D13, T5, IR[6], IR[10]);
  or or_29 (or_29_out, T0, T2);
  assign IREN = or_29_out ? 1'b1 : 1'bz;  // Controlled_Buffer controlled_buffer_15
  Decoder #(.select(2), .enable("false")) decoder_2 (
    .out0(decoder_2_out3[3]), .out1(decoder_2_out3[2]), .out2(decoder_2_out3[1]), .out3(decoder_2_out3[0]),
    .sel(IR[9:8]));
  and and_94 (and_94_out, D4, T5, IR[2], ~IR[6], IR[10]);  // AND_Gate
  and and_95 (and_95_out, D13, T4, ~IR[6], IR[10]);  // AND_Gate
  and and_96 (and_96_out, D14, T4, ~IR[6], IR[10]);  // AND_Gate
  assign DecodedIR98 = ~decoder_2_out3;  // NOT_Gate not_2, 4 bits wide
  Decoder #(.select(2), .enable("false")) decoder_3 (
    .out0(decoder_3_out3[3]), .out1(decoder_3_out3[2]), .out2(decoder_3_out3[1]), .out3(decoder_3_out3[0]),
    .sel(IR[5:4]));
  and and_97 (and_97_out, D12, T5, IR[10]);
  and and_98 (and_98_out, D5, T5, IR[2], ~IR[6], IR[10]);  // AND_Gate
  and and_99 (and_99_out, D7, T5, IR[2], ~IR[6], IR[10]);  // AND_Gate
  and and_100 (and_100_out, D8, T5, IR[2], ~IR[6], IR[10]);  // AND_Gate
  xor xor_3 (xor_3_out, IR[6], IR[2]);
  or or_30 (or_30_out, IR[6], IR[10]);
  or or_31 (or_31_out, D15, D2);
  or or_32 (or_32_out, T0, T2);
  and and_101 (and_101_out, D13, T5, ~IR[6], IR[10]);  // AND_Gate
  and and_102 (and_102_out, D14, T5, ~IR[6], IR[10]);  // AND_Gate
  and and_103 (and_103_out, D1, T4, IR[10]);
  and and_104 (and_104_out, D1, T4, ~IR[10]);  // AND_Gate
  and and_105 (and_105_out, D4_D5_D7_D8, T4, IR[6], IR[2]);
  and and_106 (and_106_out, D4_D5_D7_D8, T5, xor_3_out);
  and and_107 (and_107_out, D4_D5_D7_D8, T6, ~IR[6], ~IR[2]);  // AND_Gate
  and and_108 (and_108_out, D3_D6_D9_D10, T4, or_30_out);
  and and_109 (and_109_out, D3_D6_D9_D10, T5, ~IR[6], ~IR[10]);  // AND_Gate
  and and_110 (and_110_out, D11, T6);
  and and_111 (and_111_out, D0_D12_D13_D14, T5);
  and and_112 (and_112_out, or_31_out, T4);
  assign FunselIR = or_32_out ? 2'b10 : 2'bz;  // Controlled_Buffer controlled_buffer_16
  or or_33 (DecodedIR54ARF[1], IR[4], ~IR[5]);  // OR_Gate
  nand nand_1 (DecodedIR54ARF[0], IR[4], IR[5]);
  or or_34 (DecodedIR98ARF[1], IR[8], ~IR[9]);  // OR_Gate
  nand nand_2 (DecodedIR98ARF[0], IR[8], IR[9]);
  assign DecodedIR54 = ~decoder_3_out3;  // NOT_Gate not_3, 4 bits wide
  or or_35 (or_35_out, and_103_out, and_104_out, and_105_out, and_106_out, and_107_out, and_108_out, and_109_out, and_110_out, and_111_out, and_112_out);
  assign SC = or_35_out ? 1'b1 : 1'bz;  // Controlled_Buffer controlled_buffer_17
  and and_113 (and_113_out, D2, T4);
  and and_114 (and_114_out, D3, T4, IR[6], ~IR[10]);  // AND_Gate
  and and_115 (and_115_out, D4, T4, IR[2], IR[6], ~IR[10]);  // AND_Gate
  and and_116 (and_116_out, D5, T4, IR[2], IR[6], ~IR[10]);  // AND_Gate
  and and_117 (and_117_out, D6, T4, IR[6], ~IR[10]);  // AND_Gate
  and and_118 (and_118_out, D7, T4, IR[2], IR[6], ~IR[10]);  // AND_Gate
  and and_119 (and_119_out, D14, T4, IR[6], ~IR[10]);  // AND_Gate
  and and_120 (and_120_out, D15, T4);
  and and_121 (and_121_out, D0, T4);
  and and_122 (and_122_out, D3, T4, ~IR[6], ~IR[10]);  // AND_Gate
  and and_123 (and_123_out, D9, T4, ~IR[6], ~IR[10]);  // AND_Gate
  and and_124 (and_124_out, D4, T4, ~IR[2], IR[6], IR[10]);  // AND_Gate
  and and_125 (and_125_out, D4, T4, IR[2], ~IR[6], ~IR[10]);  // AND_Gate
  and and_126 (and_126_out, D5, T4, ~IR[2], IR[6], IR[10]);  // AND_Gate
  and and_127 (and_127_out, D5, T4, IR[2], ~IR[6], ~IR[10]);  // AND_Gate
  and and_128 (and_128_out, D7, T4, ~IR[2], IR[6], IR[10]);  // AND_Gate
  and and_129 (and_129_out, D7, T4, IR[2], ~IR[6], ~IR[10]);  // AND_Gate
  and and_130 (and_130_out, D8, T4, ~IR[2], IR[6], IR[10]);  // AND_Gate
  and and_131 (and_131_out, D8, T4, IR[2], ~IR[6], ~IR[10]);  // AND_Gate
  or or_36 (or_36_out, D4, D5, D7, D8);
  and and_132 (and_132_out, D8, T4, IR[2], IR[6], ~IR[10]);  // AND_Gate
  and and_133 (and_133_out, D9, T4, IR[6], ~IR[10]);  // AND_Gate
  and and_134 (and_134_out, D10, T4, IR[6], ~IR[10]);  // AND_Gate
  and and_135 (and_135_out, D11, T4, IR[6]);
  and and_136 (and_136_out, D12, T4);
  and and_137 (and_137_out, D13, T4, IR[6], ~IR[10]);  // AND_Gate
  and and_138 (and_138_out, D13, T4, ~IR[6], ~IR[10]);  // AND_Gate
  and and_139 (and_139_out, D14, T4, ~IR[6], ~IR[10]);  // AND_Gate
  and and_140 (and_140_out, or_36_out, T6, ~IR[6], IR[10], ~IR[2]);  // AND_Gate
  and and_141 (and_141_out, D6, T4, ~IR[6], ~IR[10]);  // AND_Gate
  and and_142 (and_142_out, D10, T4, ~IR[6], ~IR[10]);  // AND_Gate
  and and_143 (and_143_out, D4, T4, IR[2], ~IR[6], IR[10]);  // AND_Gate
  and and_144 (and_144_out, D4, T4, ~IR[2], ~IR[6], ~IR[10]);  // AND_Gate
  and and_145 (and_145_out, D5, T4, IR[2], ~IR[6], IR[10]);  // AND_Gate
  and and_146 (and_146_out, D5, T4, ~IR[2], ~IR[6], ~IR[10]);  // AND_Gate
  and and_147 (and_147_out, D7, T4, IR[2], ~IR[6], IR[10]);  // AND_Gate
  and and_148 (and_148_out, D8, T4, IR[2], ~IR[6], IR[10]);  // AND_Gate
  and and_149 (and_149_out, D11, T4, ~IR[6]);  // AND_Gate
  and and_150 (and_150_out, D5, T4, ~IR[2], ~IR[6], IR[10]);  // AND_Gate
  and and_151 (and_151_out, D7, T4, ~IR[2], ~IR[6], ~IR[10]);  // AND_Gate
  and and_152 (and_152_out, D8, T4, ~IR[2], ~IR[6], ~IR[10]);  // AND_Gate
  nand nand_3 (nand_3_out, and_132_out, and_113_out, and_133_out, and_114_out, and_115_out, and_134_out, and_116_out, and_135_out, and_136_out, and_117_out, and_137_out, and_118_out, and_138_out, and_119_out, and_139_out, and_120_out);
  and and_153 (and_153_out, D12, T5, IR[10]);
  and and_154 (and_154_out, D4, T4, ~IR[2], ~IR[6], IR[10]);  // AND_Gate
  and and_155 (and_155_out, D7, T4, ~IR[2], ~IR[6], IR[10]);  // AND_Gate
  and and_156 (and_156_out, D8, T4, ~IR[2], ~IR[6], IR[10]);  // AND_Gate
  and and_157 (and_157_out, T4, nand_3_out);
  and and_158 (and_158_out, D1, T4, ~IR[10]);  // AND_Gate
  or or_37 (or_37_out, D4, D5, D7, D8);
  or or_38 (or_38_out, D4, D5, D7, D8);
  or or_39 (or_39_out, D4, D5, D7, D8);
  or or_40 (or_40_out, D4, D5, D7, D8);
  or or_41 (or_41_out, and_121_out, and_141_out, and_149_out, and_142_out, and_122_out, and_123_out);
  and and_159 (and_159_out, D5, T4, ~IR[2], IR[6], ~IR[10]);  // AND_Gate
  and and_160 (and_160_out, or_37_out, T5, IR[6], IR[10], ~IR[2]);  // AND_Gate
  and and_161 (and_161_out, or_38_out, T5, ~IR[6], IR[10], IR[2]);  // AND_Gate
  and and_162 (and_162_out, or_39_out, T5, ~IR[6], IR[10], ~IR[2]);  // AND_Gate
  and and_163 (and_163_out, or_40_out, T5, ~IR[6], ~IR[10], ~IR[2]);  // AND_Gate
  or or_42 (or_42_out, or_41_out, or_43_out, or_44_out, or_45_out, or_46_out);
  and and_164 (and_164_out, D4, T4, ~IR[2], IR[6], ~IR[10]);  // AND_Gate
  and and_165 (and_165_out, D7, T4, ~IR[2], IR[6], ~IR[10]);  // AND_Gate
  and and_166 (and_166_out, D8, T4, ~IR[2], IR[6], ~IR[10]);  // AND_Gate
  assign TempSel = or_42_out ? 4'b0111 : 4'bz;  // Controlled_Buffer controlled_buffer_18
  or or_43 (or_43_out, and_124_out, and_154_out, and_164_out, and_143_out, and_125_out, and_144_out);
  or or_44 (or_44_out, and_126_out, and_150_out, and_159_out, and_145_out, and_127_out, and_146_out);
  or or_45 (or_45_out, and_128_out, and_155_out, and_165_out, and_147_out, and_129_out, and_151_out);
  or or_46 (or_46_out, and_130_out, and_156_out, and_166_out, and_148_out, and_131_out, and_152_out);
  and and_167 (and_167_out, D13, T5, IR[6], IR[10]);
  and and_168 (and_168_out, D13, T5, ~IR[6], IR[10]);  // AND_Gate
  and and_169 (and_169_out, D14, T5, IR[6], IR[10]);
  and and_170 (and_170_out, D14, T5, ~IR[6], IR[10]);  // AND_Gate
  assign TempSel = or_50_out ? 4'b1011 : 4'bz;  // Controlled_Buffer controlled_buffer_19
  or or_47 (or_47_out, and_157_out, and_158_out, and_160_out, and_161_out, and_162_out, and_163_out, and_153_out, and_140_out);
  assign FunSelRF = or_47_out ? 2'b10 : 2'bz;  // Controlled_Buffer controlled_buffer_20
  or or_48 (or_48_out, and_167_out, and_168_out);
  assign FunSelRF = or_48_out ? 2'b01 : 2'bz;  // Controlled_Buffer controlled_buffer_21
  assign FunSelRF = or_49_out ? 2'b00 : 2'bz;  // Controlled_Buffer controlled_buffer_22
  or or_49 (or_49_out, and_169_out, and_170_out);
  and and_171 (and_171_out, D4, T5, ~IR[2], ~IR[6], IR[10]);  // AND_Gate
  and and_172 (and_172_out, D4, T5, ~IR[2], ~IR[6], ~IR[10]);  // AND_Gate
  and and_173 (and_173_out, D7, T5, ~IR[2], ~IR[6], IR[10]);  // AND_Gate
  and and_174 (and_174_out, D7, T5, ~IR[2], ~IR[6], ~IR[10]);  // AND_Gate
  Decoder #(.select(4), .enable("false")) decoder_4 (
    .out0(D0), .out1(D1), .out2(D2), .out3(D3), .out4(D4), .out5(D5), .out6(D6), .out7(D7), .out8(D8),
    .out9(D9), .out10(D10), .out11(D11), .out12(D12), .out13(D13), .out14(D14), .out15(D15), .sel(IR[15:12]));
  and and_175 (and_175_out, D5, T5, ~IR[2], ~IR[6], ~IR[10]);  // AND_Gate
  and and_176 (and_176_out, D5, T5, ~IR[2], ~IR[6], IR[10]);  // AND_Gate
  and and_177 (and_177_out, D8, T5, ~IR[2], ~IR[6], IR[10]);  // AND_Gate
  and and_178 (and_178_out, D8, T5, ~IR[2], ~IR[6], ~IR[10]);  // AND_Gate
  or or_50 (or_50_out, and_176_out, and_171_out, and_172_out, and_175_out, and_173_out, and_177_out, and_174_out, and_178_out);
  and and_179 (and_179_out, D3, ~IR[10]);  // AND_Gate
  and and_180 (and_180_out, T4, IR[6], IR[2]);
  and and_181 (and_181_out, T5, IR[6], ~IR[2]);  // AND_Gate
  and and_182 (and_182_out, T5, ~IR[6], IR[2]);  // AND_Gate
  and and_183 (and_183_out, T6, ~IR[6], ~IR[2]);  // AND_Gate
  and and_184 (and_184_out, T6, IR[6], IR[2]);
  and and_185 (and_185_out, D5, T5);
  and and_186 (and_186_out, IR[10], ~IR[2]);  // AND_Gate
  and and_187 (and_187_out, IR[6], ~IR[2]);  // AND_Gate
  and and_188 (and_188_out, ~IR[6], IR[2]);  // AND_Gate
  and and_189 (and_189_out, D5, T4, IR[6], IR[2]);
  and and_190 (and_190_out, D5, T6, IR[6], IR[2], IR[10]);
  and and_191 (and_191_out, T4, IR[6]);
  and and_192 (and_192_out, T5, ~IR[6], ~IR[10]);  // AND_Gate
  and and_193 (and_193_out, T6, ~IR[6], ~IR[2]);  // AND_Gate
  and and_194 (and_194_out, T5, IR[6], ~IR[2]);  // AND_Gate
  and and_195 (and_195_out, T5, ~IR[6], IR[2]);  // AND_Gate
  and and_196 (and_196_out, T4, IR[6], IR[2]);
  and and_197 (and_197_out, D8, T5, ~IR[6], IR[2]);  // AND_Gate
  and and_198 (and_198_out, D8, T5, IR[6], ~IR[2]);  // AND_Gate
  and and_199 (and_199_out, D8, T4, IR[6], IR[2]);
  and and_200 (and_200_out, D8, T6, ~IR[6], ~IR[2]);  // AND_Gate
  and and_201 (and_201_out, T4, IR[6]);
  and and_202 (and_202_out, T5, ~IR[6], ~IR[10]);  // AND_Gate
  and and_203 (and_203_out, T4, IR[6]);
  and and_204 (and_204_out, T5, ~IR[6], ~IR[10]);  // AND_Gate
  or or_51 (D3_D13_D14, D13, D14, D3);
  and and_205 (and_205_out, ~IR[6], or_52_out);  // AND_Gate
  or or_52 (or_52_out, and_179_out, D11);
  and and_206 (and_206_out, and_185_out, or_53_out);
  or or_53 (or_53_out, and_186_out, and_187_out, and_188_out);
  and and_207 (and_207_out, D6, or_54_out);
  or or_54 (or_54_out, and_191_out, and_192_out);
  or or_55 (or_55_out, and_193_out, and_194_out, and_195_out, and_196_out);
  and and_208 (and_208_out, D10, or_56_out);
  assign OutputFunSelAlu = and_208_out ? 4'b1010 : 4'bz;  // Controlled_Buffer controlled_buffer_23
  or or_56 (or_56_out, and_201_out, and_202_out);
  and and_209 (and_209_out, D9, or_57_out);
  assign OutputFunSelAlu = and_209_out ? 4'b1011 : 4'bz;  // Controlled_Buffer controlled_buffer_24
  or or_57 (or_57_out, and_203_out, and_204_out);
  and and_210 (and_210_out, T4, IR[6], D3_D13_D14);
  and and_211 (and_211_out, T4, IR[6], D11);
  and and_212 (and_212_out, T5, or_58_out);
  or or_58 (or_58_out, D0, and_205_out);
  and and_213 (and_213_out, D2, T4);
  and and_214 (and_214_out, D4, or_59_out);
  assign OutputFunSelAlu = and_214_out ? 4'b0111 : 4'bz;  // Controlled_Buffer controlled_buffer_25
  or or_59 (or_59_out, and_180_out, and_181_out, and_182_out, and_183_out, and_184_out);
  or or_60 (or_60_out, and_206_out, and_189_out, and_190_out);
  assign OutputFunSelAlu = and_207_out ? 4'b0010 : 4'bz;  // Controlled_Buffer controlled_buffer_26
  and and_215 (and_215_out, D7, or_55_out);
  assign OutputFunSelAlu = and_215_out ? 4'b0100 : 4'bz;  // Controlled_Buffer controlled_buffer_27
  or or_61 (or_61_out, and_197_out, and_198_out, and_199_out, and_200_out);
  assign OutputFunSelAlu = or_61_out ? 4'b0110 : 4'bz;  // Controlled_Buffer controlled_buffer_28
  or or_62 (or_62_out, and_210_out, and_211_out, and_212_out, and_213_out);
  assign OutputFunSelAlu = or_62_out ? 4'b0000 : 4'bz;  // Controlled_Buffer controlled_buffer_29
  assign OutputFunSelAlu = or_60_out ? 4'b1000 : 4'bz;  // Controlled_Buffer controlled_buffer_30
  and and_216 (and_216_out, T5, ~IR[6], ~IR[2], D4_D5_D7_D8);  // AND_Gate
  and and_217 (and_217_out, D1, IR[10]);
  and and_218 (and_218_out, D12, IR[10]);
  or or_63 (or_63_out, ~IR[6], ~IR[2]);  // OR_Gate
  and and_219 (and_219_out, T4, IR[10], IR[6], IR[2]);
  and and_220 (and_220_out, T5, IR[10], IR[6], ~IR[2]);  // AND_Gate
  and and_221 (and_221_out, T5, IR[10], ~IR[6], IR[2]);  // AND_Gate
  and and_222 (and_222_out, T6, IR[10], ~IR[6], ~IR[2]);  // AND_Gate
  and and_223 (and_223_out, T4, IR[10], IR[6]);
  or or_64 (or_64_out, D13, D14);
  or or_65 (D4_D5_D7_D8, D4, D5, D7, D8);
  and and_224 (and_224_out, T4, or_66_out);
  or or_66 (or_66_out, D0, and_217_out);
  and and_225 (and_225_out, T5, and_218_out);
  and and_226 (and_226_out, D1, T4, ~IR[10]);  // AND_Gate
  and and_227 (and_227_out, T4, or_63_out, D4_D5_D7_D8);
  and and_228 (and_228_out, T4, ~IR[6]);  // AND_Gate
  and and_229 (and_229_out, and_219_out, D4_D5_D7_D8);
  and and_230 (and_230_out, and_220_out, D4_D5_D7_D8);
  and and_231 (and_231_out, and_221_out, D4_D5_D7_D8);
  and and_232 (and_232_out, and_222_out, D4_D5_D7_D8);
  and and_233 (and_233_out, and_223_out, D3_D6_D9_D10_D13_D14);
  or or_67 (or_67_out, D3, D6, D9, D10, D11);
  or or_68 (D3_D6_D9_D10_D11_D13IR10_D14IR10, or_67_out, and_234_out);
  and and_234 (and_234_out, or_64_out, IR[10]);
  or or_69 (D3_D6_D9_D10_D13_D14, D3, D6, D9, D10, D13, D14);
  assign OutputMuxASel = and_224_out ? 2'b11 : 2'bz;  // Controlled_Buffer controlled_buffer_31
  or or_70 (or_70_out, and_225_out, and_226_out);
  assign OutputMuxASel = or_70_out ? 2'b10 : 2'bz;  // Controlled_Buffer controlled_buffer_32
  or or_71 (or_71_out, and_227_out, and_216_out, and_235_out);
  assign OutputMuxASel = or_71_out ? 2'b01 : 2'bz;  // Controlled_Buffer controlled_buffer_33
  and and_235 (and_235_out, and_228_out, D3_D6_D9_D10_D11_D13IR10_D14IR10);
  or or_72 (or_72_out, and_229_out, and_230_out, and_231_out, and_232_out, and_233_out);
  assign OutputMuxASel = or_72_out ? 2'b00 : 2'bz;  // Controlled_Buffer controlled_buffer_34
  and and_236 (and_236_out, ~IR[10], IR[6], T4);  // AND_Gate
  or or_73 (or_73_out, D3, D6, D9, D10);
  and and_237 (and_237_out, and_236_out, or_73_out);
  and and_238 (and_238_out, T4, ~IR[10], ~IR[6]);  // AND_Gate
  or or_74 (or_74_out, D13, D14);
  and and_239 (and_239_out, D0, T5);
  and and_240 (and_240_out, IR[6], ~IR[10], T4);  // AND_Gate
  or or_75 (or_75_out, D13, D14);
  and and_241 (and_241_out, ~IR[10], IR[6], IR[2], T4);  // AND_Gate
  and and_242 (and_242_out, ~IR[10], IR[6], ~IR[2], T5);  // AND_Gate
  and and_243 (and_243_out, ~IR[10], ~IR[6], IR[2], T5);  // AND_Gate
  and and_244 (and_244_out, ~IR[10], ~IR[6], ~IR[2], T6);  // AND_Gate
  and and_245 (and_245_out, ~IR[10], ~IR[6], T5);  // AND_Gate
  or or_76 (or_76_out, D3, D6, D9, D10);
  or or_77 (D4_D5_D7_D8, D4, D5, D7, D8);
  and and_246 (and_246_out, and_238_out, or_74_out);
  assign OutputMuxBSel = and_246_out ? 2'b00 : 2'bz;  // Controlled_Buffer controlled_buffer_35
  and and_247 (and_247_out, and_240_out, or_75_out);
  and and_248 (and_248_out, and_241_out, D4_D5_D7_D8);
  and and_249 (and_249_out, and_242_out, D4_D5_D7_D8);
  and and_250 (and_250_out, and_243_out, D4_D5_D7_D8);
  and and_251 (and_251_out, and_244_out, D4_D5_D7_D8);
  and and_252 (and_252_out, and_245_out, or_76_out);
  and and_253 (and_253_out, T4, D15);
  assign OutputMuxBSel = and_253_out ? 2'b11 : 2'bz;  // Controlled_Buffer controlled_buffer_36
  assign OutputMuxBSel = and_254_out ? 2'b10 : 2'bz;  // Controlled_Buffer controlled_buffer_37
  and and_254 (and_254_out, D12, T5, ~IR[10]);  // AND_Gate
  or or_78 (or_78_out, and_247_out, and_239_out, and_248_out, and_249_out, and_250_out, and_251_out, and_252_out, and_237_out);
  assign OutputMuxBSel = or_78_out ? 2'b01 : 2'bz;  // Controlled_Buffer controlled_buffer_38
  and and_255 (and_255_out, D8, T5, IR[6], ~IR[2]);  // AND_Gate
  and and_256 (and_256_out, D8, T6, ~IR[6], ~IR[6]);  // AND_Gate
  and and_257 (and_257_out, D11, IR[6], T4);
  and and_258 (and_258_out, IR[10], IR[6], T4);
  or or_79 (or_79_out, D3, D6, D9, D10, D14, D13);
  and and_259 (and_259_out, ~IR[10], IR[6], T4);  // AND_Gate
  or or_80 (or_80_out, D3, D6, D9, D10, D14, D13);
  and and_260 (and_260_out, IR[10], IR[6], IR[2], T4);
  or or_81 (or_81_out, D4, D5, D7, D8);
  and and_261 (and_261_out, ~IR[10], IR[6], IR[2], T4);  // AND_Gate
  or or_82 (or_82_out, D4, D5, D7, D8);
  and and_262 (and_262_out, IR[10], ~IR[6], IR[2], T5);  // AND_Gate
  or or_83 (or_83_out, D4, D5, D7);
  and and_263 (and_263_out, IR[10], IR[6], ~IR[2], T5);  // AND_Gate
  or or_84 (or_84_out, D4, D5, D7, D8);
  or or_85 (or_85_out, D4, D5, D7, D8);
  and and_264 (and_264_out, D4, IR[2]);
  and and_265 (and_265_out, D5, IR[2]);
  and and_266 (and_266_out, D7, IR[2]);
  and and_267 (and_267_out, D8, IR[2]);
  and and_268 (and_268_out, ~IR[6], ~IR[2], T6, IR[10]);  // AND_Gate
  and and_269 (and_269_out, ~IR[6], ~IR[2], T6, ~IR[10]);  // AND_Gate
  or or_86 (or_86_out, D4, D5, D7);
  and and_270 (and_270_out, T4, ~IR[6], ~IR[2]);  // AND_Gate
  and and_271 (and_271_out, T4, IR[6], ~IR[2]);  // AND_Gate
  and and_272 (and_272_out, T4, D11, ~IR[6]);  // AND_Gate
  and and_273 (and_273_out, T4, ~IR[6]);  // AND_Gate
  and and_274 (and_274_out, T5, ~IR[2]);  // AND_Gate
  and and_275 (and_275_out, T4, IR[2]);
  or or_87 (D4_D5_D7_D8, D4, D5, D7, D8);
  or or_88 (D3_D6_D9_D10_D13_D14, D3, D6, D9, D10, D13, D14);
  and and_276 (and_276_out, and_258_out, or_79_out);
  and and_277 (and_277_out, and_259_out, or_80_out);
  and and_278 (and_278_out, and_260_out, or_81_out);
  and and_279 (and_279_out, and_261_out, or_82_out);
  and and_280 (and_280_out, D2, T4);
  and and_281 (and_281_out, ~IR[6], D11, T5);  // AND_Gate
  and and_282 (and_282_out, D0, T5);
  and and_283 (and_283_out, and_262_out, or_83_out);
  and and_284 (and_284_out, and_263_out, or_84_out);
  and and_285 (and_285_out, ~IR[10], IR[6], ~IR[2], T5);  // AND_Gate
  and and_286 (and_286_out, and_285_out, or_85_out);
  and and_287 (and_287_out, ~IR[10], ~IR[6], T5);  // AND_Gate
  and and_288 (and_288_out, and_287_out, or_89_out);
  or or_89 (or_89_out, and_264_out, and_265_out, and_266_out, and_267_out, D3, D6, D9, D10);
  or or_90 (or_90_out, and_268_out, and_269_out);
  and and_289 (and_289_out, or_90_out, or_86_out);
  and and_290 (and_290_out, and_270_out, D4_D5_D7_D8);
  or or_91 (or_91_out, and_290_out, and_291_out);
  assign OutputCSel = or_91_out ? IR[1:0] : 2'bz;  // Controlled_Buffer controlled_buffer_39
  and and_291 (and_291_out, and_271_out, D4_D5_D7_D8);
  or or_92 (or_92_out, and_274_out, and_275_out);
  or or_93 (or_93_out, and_257_out, and_276_out, and_277_out);
  assign OutputASel = or_93_out ? {1'b0, IR[5:4]} : 3'bz;  // Controlled_Buffer controlled_buffer_40
  or or_94 (or_94_out, and_278_out, and_255_out, and_279_out);
  assign OutputASel = or_94_out ? {1'b0, IR[1:0]} : 3'bz;  // Controlled_Buffer controlled_buffer_41
  assign OutputASel = and_280_out ? {1'b0, IR[9:8]} : 3'bz;  // Controlled_Buffer controlled_buffer_42
  assign OutputASel = and_289_out ? 3'b101 : 3'bz;  // Controlled_Buffer controlled_buffer_43
  and and_292 (and_292_out, and_273_out, D3_D6_D9_D10_D13_D14);
  or or_95 (or_95_out, and_272_out, and_292_out, and_293_out);
  and and_293 (and_293_out, or_92_out, ~IR[6], D4_D5_D7_D8);  // AND_Gate
  or or_96 (or_96_out, and_281_out, and_282_out, and_283_out, and_256_out, and_284_out, and_286_out, and_288_out);
  assign OutputASel = or_96_out ? 3'b100 : 3'bz;  // Controlled_Buffer controlled_buffer_44
  assign OutputCSel = or_95_out ? IR[5:4] : 2'bz;  // Controlled_Buffer controlled_buffer_45
  and and_294 (and_294_out, D2, T4);
  and and_295 (and_295_out, D1, ~IR[10], T4);  // AND_Gate
  or or_97 (D4___D5___D7_D8, D4, D5, D7, D8);
  or or_98 (D4___D5___D7, D4, D5, D7);
  or or_99 (or_99_out, T0, T2);
  or or_100 (or_100_out, and_294_out, and_295_out);
  and and_296 (and_296_out, D11, IR[6], T4);
  and and_297 (and_297_out, D12, T5);
  and and_298 (and_298_out, D11, ~IR[6], T5);  // AND_Gate
  and and_299 (and_299_out, T5, ~IR[10], ~IR[6], IR[2], D8);  // AND_Gate
  assign OutputDSel = or_99_out ? 2'b00 : 2'bz;  // Controlled_Buffer controlled_buffer_46
  assign OutputDSel = or_100_out ? 2'b10 : 2'bz;  // Controlled_Buffer controlled_buffer_47
  or or_101 (or_101_out, and_296_out, and_297_out, and_298_out);
  assign OutputDSel = or_101_out ? 2'b11 : 2'bz;  // Controlled_Buffer controlled_buffer_48
  and and_300 (and_300_out, T5, IR[10], IR[6], ~IR[2], D8);  // AND_Gate
  and and_301 (and_301_out, T6, ~IR[6], ~IR[2]);  // AND_Gate
  and and_302 (and_302_out, and_301_out, D4___D5___D7);
  and and_303 (and_303_out, T4, IR[10], IR[6], IR[2]);
  and and_304 (and_304_out, and_303_out, D4___D5___D7_D8);
  and and_305 (and_305_out, T5, IR[10], IR[6], ~IR[2]);  // AND_Gate
  and and_306 (and_306_out, and_305_out, D4___D5___D7_D8);
  and and_307 (and_307_out, T4, ~IR[10], IR[6], IR[2]);  // AND_Gate
  and and_308 (and_308_out, and_307_out, D4___D5___D7_D8);
  and and_309 (and_309_out, T5, ~IR[10], IR[6], ~IR[2]);  // AND_Gate
  and and_310 (and_310_out, and_309_out, D4___D5___D7_D8);
  and and_311 (and_311_out, T5, ~IR[10], ~IR[6], IR[2]);  // AND_Gate
  and and_312 (and_312_out, and_311_out, D4___D5___D7);
  and and_313 (and_313_out, T5, IR[10], ~IR[6], IR[2]);  // AND_Gate
  and and_314 (and_314_out, and_313_out, D4___D5___D7);
  or or_102 (or_102_out, and_299_out, and_300_out, and_302_out);
  and and_315 (and_315_out, T6, IR[10], ~IR[6], ~IR[2], D8);  // AND_Gate
  and and_316 (and_316_out, T6, ~IR[10], ~IR[6], ~IR[2], D8);  // AND_Gate
  or or_103 (or_103_out, and_312_out, and_314_out);
  assign OutputBSel = or_102_out ? 3'b100 : 3'bz;  // Controlled_Buffer controlled_buffer_49
  or or_104 (or_104_out, and_304_out, and_306_out, and_308_out, and_310_out);
  assign OutputBSel = or_104_out ? {1'b0, IR[5:4]} : 3'bz;  // Controlled_Buffer controlled_buffer_50
  assign OutputBSel = or_103_out ? {1'b0, IR[1:0]} : 3'bz;  // Controlled_Buffer controlled_buffer_51
  or or_105 (or_105_out, and_315_out, and_316_out);
  assign OutputBSel = or_105_out ? 3'b101 : 3'bz;  // Controlled_Buffer controlled_buffer_52

  // Other names for the same wires on the sheet: DecodedIR98ARF[2] = IR[9]; DecodedIR54ARF[2] = IR[5];
  //   FunSel_RF[1:0] = FunSelRF; FunSelAlu[3:0] = OutputFunSelAlu; MuxASel[1:0] = OutputMuxASel;
  //   MuxBSel[1:0] = OutputMuxBSel; OutASel[2:0] = OutputASel; OutBSel[2:0] = OutputBSel; OutCSel[1:0] = OutputCSel;
  //   OutDSel[1:0] = OutputDSel

  // Notes on the sheet:
  //   D4
  //   D5
  //   D7
  //   D8
  //   FunSelARF
  //   D3
  //   D9
  //   D6
  //   D10
  //   RegSelRF
  //   RegSelARF
  //   Store
  //   Load
  //   D3
  //   D9
  //   D4
  //   D5
  //   D7
  //   D8
  //   D6
  //   D10
  //   SC
  //   D5
  //   FunSel RF
  //   Tempsel
  //   D4
  //   D7
  //   D8
  //   D5
  //   OPCODE
  //   FUNSEL ALU
  //   MUX A SEL
  //   MUX B SEL
  //   OUT A SEL
  //   OUT C SEL
  //   OUT D SEL
  //   OUT B SEL
endmodule
