// Logisim project operations.circ as structural Verilog: 1 circuit, main circuit main
module main (
  input  Cin,
  input  [7:0] A,
  input  [7:0] B,
  output [7:0] A___B,
  output A___B_COUT,
  output [7:0] A___B___Carry,
  output A___B___cin_COUT,
  output [7:0] A___B_2,
  output A___B_COUT_2,
  output [7:0] A_or_B,
  output [7:0] A_and_B,
  output [7:0] A_xor_B
);

  wire [7:0] not_1_out;

  assign not_1_out = ~B;  // NOT_Gate not_1, 8 bits wide
  Adder adder_1 (.a(A), .b(B), .out(A___B), .cout(A___B_COUT));  // open: cin
  Adder adder_2 (.a(B), .b(B), .out(A___B___Carry), .cin(Cin), .cout(A___B___cin_COUT));
  Adder adder_3 (.a(A), .b(not_1_out), .out(A___B_2), .cin(1'b1), .cout(A___B_COUT_2));
  assign A_or_B = B | A;  // OR_Gate or_1, 8 bits wide
  assign A_and_B = B & A;  // AND_Gate and_1, 8 bits wide
  assign A_xor_B = A ^ B;  // XOR_Gate xor_1, 8 bits wide
endmodule
