// Logisim project register_file.circ as structural Verilog: 1 circuit, main circuit registerfile
module registerfile (
  input  [7:0] I,
  input  [2:0] OutASel,
  input  [2:0] OutBSel,
  input  [1:0] FunSel,
  input  [3:0] RegSel,
  input  [3:0] TmpSel,
  input  Clock,
  output [7:0] OutA,
  output [7:0] OutB
);

  wire not_1_out, not_2_out, not_3_out, not_4_out, not_5_out, not_6_out, not_7_out, not_8_out;
  wire [7:0] R1_q, R2_q, R3_q, R4_q, T1_q, T2_q, T3_q, T4_q;

  not not_1 (not_1_out, RegSel[3]);
  not not_2 (not_2_out, RegSel[2]);
  not not_3 (not_3_out, RegSel[1]);
  not not_4 (not_4_out, RegSel[0]);
  not not_5 (not_5_out, TmpSel[3]);
  not not_6 (not_6_out, TmpSel[2]);
  not not_7 (not_7_out, TmpSel[1]);
  not not_8 (not_8_out, TmpSel[0]);
  _8bitregister R1 (.EN(not_1_out), .I(I), .FunSel(FunSel), .Clock(Clock), .Q(R1_q));
  _8bitregister R2 (.EN(not_2_out), .I(I), .FunSel(FunSel), .Clock(Clock), .Q(R2_q));
  _8bitregister R3 (.EN(not_3_out), .I(I), .FunSel(FunSel), .Clock(Clock), .Q(R3_q));
  _8bitregister R4 (.EN(not_4_out), .I(I), .FunSel(FunSel), .Clock(Clock), .Q(R4_q));
  _8bitregister T1 (.EN(not_5_out), .I(I), .FunSel(FunSel), .Clock(Clock), .Q(T1_q));
  _8bitregister T2 (.EN(not_6_out), .I(I), .FunSel(FunSel), .Clock(Clock), .Q(T2_q));
  _8bitregister T3 (.EN(not_7_out), .I(I), .FunSel(FunSel), .Clock(Clock), .Q(T3_q));
  _8bitregister T4 (.EN(not_8_out), .I(I), .FunSel(FunSel), .Clock(Clock), .Q(T4_q));
  Multiplexer #(.select(3), .width(8)) multiplexer_1 (
    .in0(R1_q), .in1(R2_q), .in2(R3_q), .in3(R4_q), .in4(T1_q), .in5(T2_q), .in6(T3_q), .in7(T4_q),
    .out(OutA), .sel(OutASel), .en(1'b1));
  Multiplexer #(.select(3), .width(8)) multiplexer_2 (
    .in0(R1_q), .in1(R2_q), .in2(R3_q), .in3(R4_q), .in4(T1_q), .in5(T2_q), .in6(T3_q), .in7(T4_q),
    .out(OutB), .sel(OutBSel), .en(1'b1));
  Hex_Digit_Display hex_digit_display_1 (.value(OutA[7:4]));  // open: dp
  Hex_Digit_Display hex_digit_display_2 (.value(OutA[3:0]));  // open: dp
  Hex_Digit_Display hex_digit_display_3 (.value(OutB[7:4]));  // open: dp
  Hex_Digit_Display hex_digit_display_4 (.value(OutB[3:0]));  // open: dp
endmodule
